# Fritzing sketch arduino (saved by Fritzing 0.9.4)

parts:
  Part1 = Arduino Mega 2560 (Rev3)
  L298N1 = L298N DC motor driver
  LED1 = LED - 3mm [color="Red (633nm)" package="3 mm [THT]"]
  Part2 = KY-015 Temperature & Humidity Sensor Module [package="Breakout board"]
  Part3 = Soil Moisture Sensor
  J1 = Piezo Speaker
  M1 = DC Motor
  M2 = DC Motor
  PIR1 = PIR sensor
  Part4 = Adafruit TSL2561 [part_number="Adafruit #439"]
  U1 = ESP8266 NodeMCU LoLin module

nets:
  N1: Part1.A0, Part3.SIG
  N2: Part1.D21/SCL, Part4.SCL
  N3: Part1.D20/SDA, Part4.SDA
  N4: Part1.D17_PWM/RX2, U1.D6
  N5: Part1.D16_PWM/TX2, U1.D5
  N6: Part1.D15/RX3, U1.TX
  N7: Part1.D14/TX3, U1.RX
  GND: Part1.GND, L298N1.GND, LED1.cathode, Part2.-, Part3.GND, J1.pin1, PIR1.GND, Part4.GND
  N8: Part1.D13_PWM, J1.pin2
  N9: Part1.D10_PWM, PIR1.SIG
  N10: Part1.D9_PWM, LED1.anode
  N11: Part1.D8_PWM, Part2.S
  VIN: Part1.5V, L298N1.12V, Part2.Vin, Part3.VCC, PIR1.VDD, Part4.VIN
  N12: Part1.D2_PWM, L298N1.ENB
  N13: Part1.D3_PWM, L298N1.IN4
  N14: Part1.D4_PWM, L298N1.IN3
  N15: Part1.D5_PWM, L298N1.IN2
  N16: Part1.D6_PWM, L298N1.IN1
  N17: Part1.D7_PWM, L298N1.ENA
  N18: L298N1.OUT1, M1.pin_2
  N19: L298N1.OUT2, M1.pin_1
  N20: L298N1.OUT3, M2.pin_2
  N21: L298N1.OUT4, M2.pin_1

custom parts:
  L298N DC motor driver: 2x DC motor driver with 78M05 positive voltage regulator (7..35 V) L298N: max 46 V, 2 A Set 5 V Enable jumper to enable 5 V regultor (needed for the L298N) and +5 V output at screw terminal or supply external +5 V at screw terminal Set ENA and/or ENB to +5 V to enable motor permanently or supply ENA and/or ENB with PWM signal IN1 and IN2 set rotation directory for motor A (OUT1/OUT2) IN2 and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
  KY-015 Temperature & Humidity Sensor Module: KY-015 temperature and humidity sensor module, provides a low-latency serial interface to measure humidity and temperature.
  Adafruit TSL2561: The TSL2561 luminosity sensor is an advanced digital light sensor, ideal for use in a wide range of light situations. Compared to low cost CdS cells, this sensor is more precise, allowing for exact lux calculations and can be configured for different gain/timing ranges to detect light ranges from up to 0.1 - 40,000+ Lux on the fly. The best part of this sensor is that it contains both infrared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
  ESP8266 NodeMCU LoLin module: ESP8266 based NodeMCU
